# Fritzing sketch SID_shield (saved by Fritzing 0.9.4)
circuit board: 8cm x 6cm
breadboards: 1

parts:
  Arduino_Micro = Arduino Micro (Rev3)
  SID = MOS6581 [package="DIP (Dual Inline) [THT]"]
  R1 = Resistor [tolerance=±5% resistance=1k package=THT]
  R2 = Resistor [tolerance=±5% resistance=470 package=THT]
  U1 = MIDI_CONN_FEMALE [package=din_5_female]
  C1 = Ceramic Capacitor [capacitance=2.2nF package="100 mil [THT, multilayer]"]
  C2 = Ceramic Capacitor [capacitance=2.2nF package="100 mil [THT, multilayer]"]
  C3 = Ceramic Capacitor [capacitance=100nF package="200 mil [THT, multilayer]"]
  C4 = Ceramic Capacitor [capacitance=100nF package="200 mil [THT, multilayer]"]
  C7 = Electrolytic Capacitor [capacitance=10µF package="100 mil [THT, electrolytic]"]
  C6 = Mica Capacitor [package="pje 5-span capacitor"]
  C5 = Mica Capacitor [package="pje 5-span capacitor"]
  J2 = Power Jack [package=power_jack_pth]
  S1 = SWITCH-DPDT [package=os]  # not connected
  VR9 = Voltage Regulator [package=to220-igo]
  VR12 = Voltage Regulator [package=to220-igo]
  TRS1 = Audio Jack (TRS) 3.5mm [package="PG203J [THT]"]

nets:
  N1: Arduino_Micro.MOSI, SID.D2
  N2: Arduino_Micro.RXLED/SS, SID.D0
  N3: Arduino_Micro.D0/RX, U1.MIDI_OUT
  N4: Arduino_Micro.D5_PWM, SID.Ø2
  N5: Arduino_Micro.D8_PWM/A8, SID.D4
  N6: Arduino_Micro.D9_PWM/A9, SID.D5
  N7: Arduino_Micro.D10_PWM/A10, SID.D6
  N8: Arduino_Micro.D11_PWM, SID.D7
  N9: Arduino_Micro.SCK, SID.D1
  N10: Arduino_Micro.MISO, SID.D3
  N11: Arduino_Micro.VIN, C4.0, VR9.OUT
  GND: Arduino_Micro.GND, SID.R/W, SID.GND, SID.EXTIN, R1.Pin_1, R2.Pin_0, C3.1, C4.1, C6.1, C5.1, J2.GND, VR9.GND, VR12.GND, TRS1.Sleeve
  5V: Arduino_Micro.5V, SID.RES, SID.VCC
  N12: Arduino_Micro.A5, SID.A0
  N13: Arduino_Micro.A4, SID.A1
  N14: Arduino_Micro.A3, SID.A2
  N15: Arduino_Micro.A2, SID.A3
  N16: Arduino_Micro.A1, SID.A4
  N17: Arduino_Micro.D13_PWM, SID.CS
  N18: SID.CAP1A, C1.0
  N19: SID.CAP1B, C1.1
  N20: SID.CAP2A, C2.0
  N21: SID.CAP2B, C2.1
  N22: SID.AUDIOOUT, R1.Pin_0, C7.+
  N23: SID.VDD, C3.0, C6.0, VR9.IN, VR12.OUT
  N24: R2.Pin_1, U1.MIDI_IN
  N25: C7.-, TRS1.Ring, TRS1.Tip
  N26: C5.0, J2.PWR, VR12.IN

custom parts:
  MOS6581: The SID. MOS6581
  Mica Capacitor: 0.22µF Mica (?) Capacitor
  Voltage Regulator: Voltage Regulator Standard 7809 9V regulator. IGO (Input Ground Output).
